# Fritzing sketch arduino-led-13 (saved by Fritzing 0.9.3b)
breadboards: 1

parts:
  Raspberry_Pi_3 = Raspberry Pi 3 [part_number=RPI-3-V1.2]  # not connected
  Arduino_101 = Arduino 101
  LED1 = smd LED [color="Yellow (592nm)" package="1206 [SMD]"]
  R1 = Resistor [tolerance=±5% resistance=470 package="2010 [SMD]"]

nets:
  N1: Arduino_101.D13/SCK, LED1.anode
  N2: Arduino_101.GND, R1.Pin_0
  N3: LED1.cathode, R1.Pin_1

custom parts:
  Arduino 101: A learning and development board that delivers the performance and low-power consumption of the Intel® Curie™ Module with the simplicity of Arduino at an entry-level price. It keeps the same robust form factor and peripheral list of the UNO with the addition of onboard Bluetooth LE capabilities and a 6-axis accelerometer/gyro to help you easily expand your creativity into the connected world.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
