# Fritzing sketch arduino101 (saved by Fritzing 0.9.3b)

parts:
  Arduino_101 = Arduino 101
  Part3 = Adafruit Si7021 Temp Humidity [part_number="Adafruit #3251"]

nets:
  N1: Arduino_101.A0, Part3.VIN
  N2: Arduino_101.A1, Part3.+3V3
  N3: Arduino_101.A2, Part3.GND
  N4: Arduino_101.A3, Part3.SCL
  N5: Arduino_101.A4/SDA, Part3.SDA

custom parts:
  Arduino 101: A learning and development board that delivers the performance and low-power consumption of the Intel® Curie™ Module with the simplicity of Arduino at an entry-level price. It keeps the same robust form factor and peripheral list of the UNO with the addition of onboard Bluetooth LE capabilities and a 6-axis accelerometer/gyro to help you easily expand your creativity into the connected world.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
  Adafruit Si7021 Temp Humidity: It's summer and you're sweating and your hair's all frizzy and all you really want to know is why the weatherman said this morning that today's relative humidity would max out at a perfectly reasonable 42% when it feels more like 77%. Enter the Si7021 Temperature + Humidity Sensor - the best way to prove the weatherman wrong! This lovely sensor for Silicon labs has ± 3% relative humidity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

// code stored in the sketch: arduino-led-9.ino
#include <CurieBLE.h>


const int pinLED = 9;

BLEPeripheral ble;
BLEService lightbulbService("8E76F000-690E-472E-88C3-051277686A73");
BLECharCharacteristic onCharacteristic("8E76F001-690E-472E-88C3-051277686A73", BLERead | BLEWrite);
BLEFloatCharacteristic brightnessCharacteristic("8E76F002-690E-472E-88C3-051277686A73", BLERead | BLEWrite);


void setup() {
  Serial.begin(115200);
  pinMode(pinLED, OUTPUT);

  ble.setLocalName("Arduino");
  ble.setAdvertisedServiceUuid(lightbulbService.uuid());

  ble.addAttribute(lightbulbService);
  ble.addAttribute(onCharacteristic);
  ble.addAttribute(brightnessCharacteristic);

  ble.setEventHandler(BLEConnected, onCentralConnect);
  ble.setEventHandler(BLEDisconnected, onCentralDisconnect);

  onCharacteristic.setValue(true);
  brightnessCharacteristic.setValue(100.0);
  setLED(true, 100.0);

  onCharacteristic.setEventHandler(BLEWritten, onCharacteristicWrite);
  brightnessCharacteristic.setEventHandler(BLEWritten, onCharacteristicWrite);
  
  
  ble.begin();
  Serial.println("Bluetooth on");
}

void loop() {
  ble.poll();
}


void onCentralConnect(BLECentral& central) {
  Serial.print("Central device connected: ");
  Serial.println(central.address());
}

void onCentralDisconnect(BLECentral& central) {
  Serial.print("Central device disconnected: ");
  Serial.println(central.address());
}

void onCharacteristicWrite(BLECentral& central, BLECharacteristic& characteristic) {
  Serial.print("Characteristic written: ");
  Serial.println(characteristic.uuid());

  bool state = (bool) onCharacteristic.value();
  float brightness = brightnessCharacteristic.value();
  setLED(state, brightness);
}

void setLED(bool state, float brightness) {
  const int analogMax = 255;
  brightness = max(0.0, min(100.0, brightness));  
 
  Serial.print("LED state: ");
  Serial.print(state);
  Serial.print("|");
  Serial.println(brightness);

  analogWrite(pinLED, int(state) * int(brightness / 100.0) * analogMax);
}

// code stored in the sketch: arduino-lightbulb.ino
#include <CurieBLE.h>


const int pinLED = 9;
const int pinSwitch = 2;

BLEPeripheral ble;
BLEService lightbulbService("8E76F000-690E-472E-88C3-051277686A73");
BLECharCharacteristic onCharacteristic("8E76F001-690E-472E-88C3-051277686A73", BLERead | BLEWrite | BLENotify);
BLEFloatCharacteristic brightnessCharacteristic("8E76F002-690E-472E-88C3-051277686A73", BLERead | BLEWrite | BLENotify);


void setup() {
  Serial.begin(115200);
  pinMode(pinLED, OUTPUT);
  pinMode(pinSwitch, INPUT_PULLUP);

  ble.setLocalName("Arduino");
  ble.setAdvertisedServiceUuid(lightbulbService.uuid());

  ble.addAttribute(lightbulbService);
  ble.addAttribute(onCharacteristic);
  ble.addAttribute(brightnessCharacteristic);

  ble.setEventHandler(BLEConnected, onCentralConnect);
  ble.setEventHandler(BLEDisconnected, onCentralDisconnect);

  onCharacteristic.setValue(true);
  brightnessCharacteristic.setValue(100.0);
  setLED(true, 100.0);
  attachInterrupt(digitalPinToInterrupt(pinSwitch), setSwitch, FALLING);

  onCharacteristic.setEventHandler(BLEWritten, onCharacteristicWrite);
  brightnessCharacteristic.setEventHandler(BLEWritten, onCharacteristicWrite);
  
  
  ble.begin();
  Serial.println("Bluetooth on");
}

void loop() {
  ble.poll();
}


void onCentralConnect(BLECentral& central) {
  Serial.print("Central device connected: ");
  Serial.println(central.address());
}

void onCentralDisconnect(BLECentral& central) {
  Serial.print("Central device disconnected: ");
  Serial.println(central.address());
}

void onCharacteristicWrite(BLECentral& central, BLECharacteristic& characteristic) {
  Serial.print("Characteristic written: ");
  Serial.println(characteristic.uuid());

  bool on = onCharacteristic.value();
  float brightness = brightnessCharacteristic.value();
  setLED(on, brightness);
}

void setLED(bool on, float brightness) {
  const int analogMax = 255;
  brightness = max(0.0, min(100.0, brightness));  
 
  Serial.print("LED state: ");
  Serial.print(on);
  Serial.print("|");
  Serial.println(brightness);

  analogWrite(pinLED, int(on) * int(brightness / 100.0) * analogMax);
}

void setSwitch(void) {
  Serial.println("Switch toggled");
  bool on = onCharacteristic.value();
  float brightness = brightnessCharacteristic.value();

  onCharacteristic.setValue(!on);
  setLED(!on, brightness);
}

// code stored in the sketch: arduino101.ino
#include <Arduino.h>
#include <CurieBLE.h>
#include <SoftwareWire.h>
#include "Si7021.h"

static struct BoardPins {
  const uint8_t VIN = A0;
  const uint8_t VO3 = A1;
  const uint8_t GND = A2;
  const uint8_t SCL = A3;
  const uint8_t SDA = A4;
} Pin;

SoftwareWire wire = SoftwareWire(Pin.SDA, Pin.SCL);
Si7021 sensor = Si7021(wire);

BLEPeripheral ble;
BLEService informationService("180A");
BLECharacteristic modelCharacteristic("2A24", BLERead, "101");
BLECharacteristic manufacturerCharacteristic("2A29", BLERead, "Arduino");
BLECharacteristic serialNumberCharacteristic("2A25", BLERead, "2.71828");

BLEService humidityService("10525F60-CF73-11E6-9598-F8E2251C9A69");
BLEFloatCharacteristic humidityCharacteristic("10525F61-CF73-11E6-9598-F8E2251C9A69", BLERead | BLENotify);
BLEService thermometerService("F489CB00-C177-11E6-9598-9854249C9A66");
BLEFloatCharacteristic temperatureCharacteristic("F489CB01-C177-11E6-9598-9854249C9A66", BLERead | BLENotify);


void setup() {
  Serial.begin(115200);
  
  pinMode(Pin.VIN, OUTPUT);
  digitalWrite(Pin.VIN, HIGH);
  pinMode(Pin.GND, OUTPUT);
  digitalWrite(Pin.GND, LOW);
  sensor.begin();

  ble.setLocalName("Humidity");
  ble.setAdvertisedServiceUuid(thermometerService.uuid());
  ble.addAttribute(informationService);
  ble.addAttribute(modelCharacteristic);
  ble.addAttribute(manufacturerCharacteristic);
  ble.addAttribute(serialNumberCharacteristic);

  ble.addAttribute(humidityService);
  ble.addAttribute(humidityCharacteristic);
  humidityCharacteristic.setValueLE(0.0);
  ble.addAttribute(thermometerService);
  ble.addAttribute(temperatureCharacteristic);
  temperatureCharacteristic.setValueLE(0.0);

  ble.setEventHandler(BLEConnected, centralConnect);
  ble.setEventHandler(BLEDisconnected, centralDisconnect);

  ble.begin();
  Serial.println("Bluetooth on");
}

void loop() {
  ble.poll();

  static float averageHumidity = sensor.readHumidity();
  averageHumidity += (sensor.readTemperature() - averageHumidity) / 30.0;
  float previousHumidity = humidityCharacteristic.valueLE();
  if (abs(averageHumidity - previousHumidity) > 0.10) {
    humidityCharacteristic.setValueLE(averageHumidity);
    Serial.print("Update temperature | ");
    Serial.println(averageHumidity, 0);
  } else {
    Serial.print("Temperature | ");
    Serial.println(averageHumidity, 0);
  }

  static float averageCelsius = sensor.readTemperature();
  averageCelsius += (sensor.readTemperature() - averageCelsius) / 30.0;
  float previousCelsius = temperatureCharacteristic.valueLE();
  if (abs(averageCelsius - previousCelsius) > 0.10) {
    temperatureCharacteristic.setValueLE(averageCelsius);
    Serial.print("Update temperature | ");
    Serial.println(averageCelsius, 2);
  } else {
    Serial.print("Temperature | ");
    Serial.println(averageCelsius, 2);
  }
  
  delay(1000);
}


void centralConnect(BLECentral& central) {
  Serial.print("Central connected | ");
  Serial.println(central.address());
}

void centralDisconnect(BLECentral& central) {
  Serial.print("Central disconnected | ");
  Serial.println(central.address());
}
