# Fritzing sketch bluefruit (saved by Fritzing 0.9.3b)

parts:
  Part2 = Adafruit Si7021 Temp Humidity [part_number="Adafruit #3251"]
  Part3 = Adafruit Bluefruit LE Micro [part_number="Adafruit #2661"]

nets:
  N1: Part2.SDA, Part3.A4
  N2: Part2.SCL, Part3.A3
  N3: Part2.GND, Part3.A2
  N4: Part2.+3V3, Part3.A1
  N5: Part2.VIN, Part3.A0

custom parts:
  Adafruit Si7021 Temp Humidity: It's summer and you're sweating and your hair's all frizzy and all you really want to know is why the weatherman said this morning that today's relative humidity would max out at a perfectly reasonable 42% when it feels more like 77%. Enter the Si7021 Temperature + Humidity Sensor - the best way to prove the weatherman wrong! This lovely sensor for Silicon labs has ± 3% relative humidity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
  Adafruit Bluefruit LE Micro: Would you like to add powerful and easy-to-use Bluetooth Low Energy to your robot, art or other electronics project? Heck yeah! With BLE now included in modern smart phones and tablets, its fun to add wireless connectivity. So what you really need is the new Adafruit Bluefruit LE Micro - it's an Atmega32u4 chip (same as used as in the Adafruit Flora or Arduino Leonardo) plus our SPI Bluefruit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

// code stored in the sketch: arduino-led-9.ino
#include <CurieBLE.h>


const int pinLED = 9;

BLEPeripheral ble;
BLEService lightbulbService("8E76F000-690E-472E-88C3-051277686A73");
BLECharCharacteristic onCharacteristic("8E76F001-690E-472E-88C3-051277686A73", BLERead | BLEWrite);
BLEFloatCharacteristic brightnessCharacteristic("8E76F002-690E-472E-88C3-051277686A73", BLERead | BLEWrite);


void setup() {
  Serial.begin(115200);
  pinMode(pinLED, OUTPUT);

  ble.setLocalName("Arduino");
  ble.setAdvertisedServiceUuid(lightbulbService.uuid());

  ble.addAttribute(lightbulbService);
  ble.addAttribute(onCharacteristic);
  ble.addAttribute(brightnessCharacteristic);

  ble.setEventHandler(BLEConnected, onCentralConnect);
  ble.setEventHandler(BLEDisconnected, onCentralDisconnect);

  onCharacteristic.setValue(true);
  brightnessCharacteristic.setValue(100.0);
  setLED(true, 100.0);

  onCharacteristic.setEventHandler(BLEWritten, onCharacteristicWrite);
  brightnessCharacteristic.setEventHandler(BLEWritten, onCharacteristicWrite);
  
  
  ble.begin();
  Serial.println("Bluetooth on");
}

void loop() {
  ble.poll();
}


void onCentralConnect(BLECentral& central) {
  Serial.print("Central device connected: ");
  Serial.println(central.address());
}

void onCentralDisconnect(BLECentral& central) {
  Serial.print("Central device disconnected: ");
  Serial.println(central.address());
}

void onCharacteristicWrite(BLECentral& central, BLECharacteristic& characteristic) {
  Serial.print("Characteristic written: ");
  Serial.println(characteristic.uuid());

  bool state = (bool) onCharacteristic.value();
  float brightness = brightnessCharacteristic.value();
  setLED(state, brightness);
}

void setLED(bool state, float brightness) {
  const int analogMax = 255;
  brightness = max(0.0, min(100.0, brightness));  
 
  Serial.print("LED state: ");
  Serial.print(state);
  Serial.print("|");
  Serial.println(brightness);

  analogWrite(pinLED, int(state) * int(brightness / 100.0) * analogMax);
}

// code stored in the sketch: arduino-lightbulb.ino
#include <CurieBLE.h>


const int pinLED = 9;
const int pinSwitch = 2;

BLEPeripheral ble;
BLEService lightbulbService("8E76F000-690E-472E-88C3-051277686A73");
BLECharCharacteristic onCharacteristic("8E76F001-690E-472E-88C3-051277686A73", BLERead | BLEWrite | BLENotify);
BLEFloatCharacteristic brightnessCharacteristic("8E76F002-690E-472E-88C3-051277686A73", BLERead | BLEWrite | BLENotify);


void setup() {
  Serial.begin(115200);
  pinMode(pinLED, OUTPUT);
  pinMode(pinSwitch, INPUT_PULLUP);

  ble.setLocalName("Arduino");
  ble.setAdvertisedServiceUuid(lightbulbService.uuid());

  ble.addAttribute(lightbulbService);
  ble.addAttribute(onCharacteristic);
  ble.addAttribute(brightnessCharacteristic);

  ble.setEventHandler(BLEConnected, onCentralConnect);
  ble.setEventHandler(BLEDisconnected, onCentralDisconnect);

  onCharacteristic.setValue(true);
  brightnessCharacteristic.setValue(100.0);
  setLED(true, 100.0);
  attachInterrupt(digitalPinToInterrupt(pinSwitch), setSwitch, FALLING);

  onCharacteristic.setEventHandler(BLEWritten, onCharacteristicWrite);
  brightnessCharacteristic.setEventHandler(BLEWritten, onCharacteristicWrite);
  
  
  ble.begin();
  Serial.println("Bluetooth on");
}

void loop() {
  ble.poll();
}


void onCentralConnect(BLECentral& central) {
  Serial.print("Central device connected: ");
  Serial.println(central.address());
}

void onCentralDisconnect(BLECentral& central) {
  Serial.print("Central device disconnected: ");
  Serial.println(central.address());
}

void onCharacteristicWrite(BLECentral& central, BLECharacteristic& characteristic) {
  Serial.print("Characteristic written: ");
  Serial.println(characteristic.uuid());

  bool on = onCharacteristic.value();
  float brightness = brightnessCharacteristic.value();
  setLED(on, brightness);
}

void setLED(bool on, float brightness) {
  const int analogMax = 255;
  brightness = max(0.0, min(100.0, brightness));  
 
  Serial.print("LED state: ");
  Serial.print(on);
  Serial.print("|");
  Serial.println(brightness);

  analogWrite(pinLED, int(on) * int(brightness / 100.0) * analogMax);
}

void setSwitch(void) {
  Serial.println("Switch toggled");
  bool on = onCharacteristic.value();
  float brightness = brightnessCharacteristic.value();

  onCharacteristic.setValue(!on);
  setLED(!on, brightness);
}

// code stored in the sketch: arduino101.ino
#include <Arduino.h>
#include <CurieBLE.h>
#include <CurieIMU.h>


BLEPeripheral ble;
BLEService informationService("180A");
BLECharacteristic modelCharacteristic("2A24", BLERead, "101");
BLECharacteristic manufacturerCharacteristic("2A29", BLERead, "Arduino");
BLECharacteristic serialNumberCharacteristic("2A25", BLERead, "2.71828");

BLEService thermometerService("1D8A68E0-E68E-4FED-943E-369099F5B499");
BLEFloatCharacteristic temperatureCharacteristic("1D8A68E1-E68E-4FED-943E-369099F5B499", BLERead | BLENotify);


void setup() {
  Serial.begin(115200);

  ble.setLocalName("Thermo");
  ble.setAdvertisedServiceUuid(thermometerService.uuid());
  ble.addAttribute(informationService);
  ble.addAttribute(modelCharacteristic);
  ble.addAttribute(manufacturerCharacteristic);
  ble.addAttribute(serialNumberCharacteristic);

  ble.addAttribute(thermometerService);
  ble.addAttribute(temperatureCharacteristic);
  temperatureCharacteristic.setValueLE(0.0);

  ble.setEventHandler(BLEConnected, centralConnect);
  ble.setEventHandler(BLEDisconnected, centralDisconnect);

  ble.begin();
  CurieIMU.begin();
  Serial.println("Bluetooth on");
}

void loop() {
  ble.poll();

  float currentCelsius = (float) CurieIMU.readTemperature() / 32767.0 + 23.0;
  float previousCelsius = temperatureCharacteristic.valueLE();
  if (abs(currentCelsius - previousCelsius) > 0.10) {
    temperatureCharacteristic.setValueLE(currentCelsius);
    Serial.print("Update temperature | ");
    Serial.println(currentCelsius);
  } else {
    Serial.print("Temperature | ");
    Serial.println(currentCelsius);
  }
  delay(1000);
}


void centralConnect(BLECentral& central) {
  Serial.print("Central connected | ");
  Serial.println(central.address());
}

void centralDisconnect(BLECentral& central) {
  Serial.print("Central disconnected | ");
  Serial.println(central.address());
}

// code stored in the sketch: bluefruit.ino
#include <SPI.h>
#include <Arduino.h>

#include <Adafruit_BLE.h>
#include <Adafruit_BLEGatt.h>
#include <Adafruit_BluefruitLE_SPI.h>

#include "Si7021.h"

static struct BoardPins {
  const uint8_t VIN = A0;
  const uint8_t VO3 = A1;
  const uint8_t GND = A2;
  const uint8_t SCL = A3;
  const uint8_t SDA = A4;
} Pin;

SoftwareWire wire = SoftwareWire(Pin.SDA, Pin.SCL);
Si7021 sensor = Si7021(wire);

Adafruit_BluefruitLE_SPI ble(8, 7, 4); // Firmware > 0.7.0
Adafruit_BLEGatt gatt(ble);
int32_t humidityService;
int32_t humidityCharacteristic;
int32_t thermometerService;
int32_t temperatureCharacteristic;

union float_bytes {
  float value;
  uint8_t bytes[sizeof(float)]; 
};


void setup(void) {
  Serial.begin(115200);

  pinMode(Pin.VIN, OUTPUT);
  digitalWrite(Pin.VIN, HIGH);
  pinMode(Pin.GND, OUTPUT);
  digitalWrite(Pin.GND, LOW);
  sensor.begin();

  ble.begin(/* true - useful for debugging */);
  ble.factoryReset();
  ble.info();

  uint8_t humidityServiceUUID[] = {0x10,0x52,0x5F,0x60,0xCF,0x73,0x11,0xE6,0x95,0x98,0xF8,0xE2,0x25,0x1C,0x9A,0x69};
  humidityService = gatt.addService(humidityServiceUUID);
  uint8_t humidityCharacteristicUUID[] = {0x10,0x52,0x5F,0x61,0xCF,0x73,0x11,0xE6,0x95,0x98,0xF8,0xE2,0x25,0x1C,0x9A,0x69};
  humidityCharacteristic = gatt.addCharacteristic(humidityCharacteristicUUID,
                                                  GATT_CHARS_PROPERTIES_READ | GATT_CHARS_PROPERTIES_NOTIFY,
                                                  sizeof(float), sizeof(float), BLE_DATATYPE_BYTEARRAY);

  uint8_t thermometerServiceUUID[] = {0xF3,0x89,0xCB,0x00,0xC1,0x77,0x11,0xE6,0x95,0x98,0x98,0x54,0x24,0x9C,0x9A,0x66};
  thermometerService = gatt.addService(thermometerServiceUUID);
  uint8_t thermometerCharacteristicUUID[] = {0xF3,0x89,0xCB,0x01,0xC1,0x77,0x11,0xE6,0x95,0x98,0x98,0x54,0x24,0x9C,0x9A,0x66};
  temperatureCharacteristic = gatt.addCharacteristic(thermometerCharacteristicUUID,
                                                     GATT_CHARS_PROPERTIES_READ | GATT_CHARS_PROPERTIES_NOTIFY,
                                                     sizeof(float), sizeof(float), BLE_DATATYPE_BYTEARRAY);


  
  ble.reset();
  ble.setConnectCallback(centralConnect);
  ble.setDisconnectCallback(centralDisconnect);
  Serial.println("Bluetooth on");
}

/** Send randomized heart rate data continuously **/
void loop(void) {
  ble.update();

  static union float_bytes averageHumidity = { .value = sensor.readHumidity() };
  averageHumidity.value += (sensor.readHumidity() - averageHumidity.value) / 30.0;
  static union float_bytes previousHumidity = { .value = 0.0 };
  gatt.getChar(humidityCharacteristic, previousHumidity.bytes, sizeof(previousHumidity));
  
  if (abs(averageHumidity.value - previousHumidity.value) > 0.10) {
    gatt.setChar(humidityCharacteristic, averageHumidity.bytes, sizeof(averageHumidity));
    Serial.print("Update humidity | ");
    Serial.println(averageHumidity.value, 0);
  } else {
    Serial.print("Humidity | ");
    Serial.println(averageHumidity.value, 0);
  }

  static union float_bytes averageCelsius = { .value = sensor.readTemperature()};
  averageCelsius.value += (sensor.readTemperature() - averageCelsius.value) / 30.0;
  static union float_bytes previousCelsius = { .value = 0.0 };
  gatt.getChar(temperatureCharacteristic, previousCelsius.bytes, sizeof(previousCelsius));
  
  if (abs(averageCelsius.value - previousCelsius.value) > 0.10) {
    gatt.setChar(temperatureCharacteristic, averageCelsius.bytes, sizeof(averageCelsius));
    Serial.print("Update temperature | ");
    Serial.println(averageCelsius.value, 2);
  } else {
    Serial.print("Temperature | ");
    Serial.println(averageCelsius.value, 2);
  }
  
  delay(1000);
}


void centralConnect(void) {
  Serial.print("Central connected | ");
  if (ble.sendCommandCheckOK("AT+BLEGETPEERADDR")) {
    Serial.println(ble.buffer);
  }
}

void centralDisconnect(void) {
  Serial.print("Central disconnected | ");
  if (ble.sendCommandCheckOK("AT+BLEGETPEERADDR")) {
    Serial.println(ble.buffer);
  }
}
