# Fritzing sketch arduino101 (saved by Fritzing 0.9.3b)
breadboards: 1

parts:
  Arduino_101 = Arduino 101
  LED1 = smd LED [color="Red (633nm)" package="1206 [SMD]"]
  LED2 = smd LED [color="Green (555nm)" package="1206 [SMD]"]
  LED3 = smd LED [color="Blue (505nm)" package="1206 [SMD]"]
  R1 = Resistor [tolerance=±5% resistance=470 package="2010 [SMD]"]
  R2 = Resistor [tolerance=±5% resistance=470 package="2010 [SMD]"]
  R3 = Resistor [tolerance=±5% resistance=470 package="2010 [SMD]"]
  S3 = Momentary Switch [package=ksa_sealed_tac_switch]

nets:
  N1: Arduino_101.D9_PWM, LED1.anode
  N2: Arduino_101.GND, R1.Pin_0, R2.Pin_0, R3.Pin_0, S3.3
  N3: Arduino_101.D2, S3.2
  N4: Arduino_101.D5_PWM, LED3.anode
  N5: Arduino_101.D6_PWM, LED2.anode
  N6: LED1.cathode, R1.Pin_1
  N7: LED2.cathode, R2.Pin_1
  N8: LED3.cathode, R3.Pin_1

custom parts:
  Arduino 101: A learning and development board that delivers the performance and low-power consumption of the Intel® Curie™ Module with the simplicity of Arduino at an entry-level price. It keeps the same robust form factor and peripheral list of the UNO with the addition of onboard Bluetooth LE capabilities and a 6-axis accelerometer/gyro to help you easily expand your creativity into the connected world.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

// code stored in the sketch: arduino101.ino
#include <math.h>
#include <Arduino.h>
#include <CurieBLE.h>

const int pinRedLED = 5;
const int pinGreenLED = 6;
const int pinBlueLED = 9;
const int pinSwitch = 2;


BLEPeripheral ble;
BLEService lightbulbService("57E54BF0-8574-47BE-9C1D-A0DBFC8FA183");
BLECharCharacteristic onCharacteristic("57E54BF1-8574-47BE-9C1D-A0DBFC8FA183", BLERead | BLEWrite | BLENotify);
BLEFloatCharacteristic hueCharacteristic("57E54BF2-8574-47BE-9C1D-A0DBFC8FA183", BLERead | BLEWrite | BLENotify);
BLEFloatCharacteristic saturationCharacteristic("57E54BF3-8574-47BE-9C1D-A0DBFC8FA183", BLERead | BLEWrite | BLENotify);
BLEIntCharacteristic brightnessCharacteristic("57E54BF4-8574-47BE-9C1D-A0DBFC8FA183", BLERead | BLEWrite | BLENotify);
bool lastSwitch = HIGH;


void setup() {
  Serial.begin(115200);
  pinMode(pinRedLED, OUTPUT);
  pinMode(pinGreenLED, OUTPUT);  
  pinMode(pinBlueLED, OUTPUT);
  pinMode(pinSwitch, INPUT_PULLUP);

  ble.setLocalName("Light");
  ble.setAdvertisedServiceUuid(lightbulbService.uuid());

  ble.addAttribute(lightbulbService);
  ble.addAttribute(onCharacteristic);
  ble.addAttribute(hueCharacteristic);
  ble.addAttribute(saturationCharacteristic);
  ble.addAttribute(brightnessCharacteristic);

  bool on = true;
  float hue = 0.0;
  float saturation = 0.0;
  int brightness = 100;
  onCharacteristic.setValueLE(on);
  hueCharacteristic.setValueLE(hue);
  saturationCharacteristic.setValueLE(saturation);
  brightnessCharacteristic.setValueLE(brightness);
  setLED(on, hue, saturation, brightness);

  ble.setEventHandler(BLEConnected, centralConnect);
  ble.setEventHandler(BLEDisconnected, centralDisconnect);
  onCharacteristic.setEventHandler(BLEWritten, characteristicWrite);
  hueCharacteristic.setEventHandler(BLEWritten, characteristicWrite);
  saturationCharacteristic.setEventHandler(BLEWritten, characteristicWrite);
  brightnessCharacteristic.setEventHandler(BLEWritten, characteristicWrite);

  ble.begin();
  Serial.println("Bluetooth on");
  lastSwitch = digitalRead(pinSwitch);
}

void loop() {
  ble.poll();

  if ((digitalRead(pinSwitch) == LOW) && (lastSwitch == HIGH)) {
    bool on = (bool) onCharacteristic.valueLE();
    float hue = (float) hueCharacteristic.valueLE();
    float saturation = (float) saturationCharacteristic.valueLE();
    int brightness = (int) brightnessCharacteristic.valueLE();
    setLED(!on, hue, saturation, brightness);
    onCharacteristic.setValue(!on);
    ble.poll();
    lastSwitch = LOW;
    delay(1);
  } else if ((digitalRead(pinSwitch) == HIGH) && (lastSwitch == LOW)) {
    lastSwitch = HIGH;
    delay(1);
  }
}

void centralConnect(BLECentral& central) {
  Serial.print("Central connected | ");
  Serial.println(central.address());
}

void centralDisconnect(BLECentral& central) {
  Serial.print("Central disconnected | ");
  Serial.println(central.address());
}

void characteristicWrite(BLECentral& central, BLECharacteristic& characteristic) {
  Serial.print("Characteristic written | ");
  Serial.println(characteristic.uuid());

  bool on = (bool) onCharacteristic.valueLE();
  float hue = (float) hueCharacteristic.valueLE();
  float saturation = (float) saturationCharacteristic.valueLE();
  int brightness = (int) brightnessCharacteristic.valueLE();
  setLED(on, hue, saturation, brightness);
}

void setLED(bool on, float hue, float saturation, int brightness) {
  hue = max(0.0, min(360.0, hue));
  saturation = max(0.0, min(100.0, saturation));
  brightness = max(0, min(100, brightness));

  unsigned int red, green, blue;
  hsv2rgb(hue, saturation/100.0, brightness/100.0, &red, &green, &blue);
  analogWrite(pinRedLED, on * red);
  analogWrite(pinGreenLED, on * green);
  analogWrite(pinBlueLED, on * blue);
  
  Serial.print("RGB LED | ");
  Serial.print(on);
  Serial.print(" HSB(");
  Serial.print(hue);
  Serial.print(",");
  Serial.print(saturation);
  Serial.print(",");
  Serial.print(brightness);
  Serial.print(") -> RGB(");
  Serial.print(red);
  Serial.print(",");
  Serial.print(green);
  Serial.print(",");
  Serial.print(blue);
  Serial.println(")");
}

void hsv2rgb(float hue, float saturation, float value,
             unsigned int* red, unsigned int* green, unsigned int* blue) {
  if (saturation == 0.0) {
    *red   = (unsigned int) round(value * 255.0);
    *green = (unsigned int) round(value * 255.0);
    *blue  = (unsigned int) round(value * 255.0);
  } else {
    int h = ((int) floor(hue / 60.0) % 6);
    float f = (hue / 60.0) - floor(hue / 60.0);
    float p = value * (1.0 - saturation);
    float q = value * (1.0 - saturation * f);
    float t = value * (1.0 - (saturation * (1.0 - f)));
    switch (h) {
      case 0:
        *red   = (unsigned int) round(value * 255.0);
        *green = (unsigned int) round(t * 255.0);
        *blue  = (unsigned int) round(p * 255.0);
        break;
      case 1:
        *red   = (unsigned int) round(q * 255.0);
        *green = (unsigned int) round(value * 255.0);
        *blue  = (unsigned int) round(p * 255.0);
        break;
      case 2:
        *red   = (unsigned int) round(p * 255.0);
        *green = (unsigned int) round(value * 255.0);
        *blue  = (unsigned int) round(t * 255.0);
        break;
      case 3:
        *red   = (unsigned int) round(p * 255.0);
        *green = (unsigned int) round(q * 255.0);
        *blue  = (unsigned int) round(value * 255.0);
        break;
      case 4:
        *red   = (unsigned int) round(t * 255.0);
        *green = (unsigned int) round(p * 255.0);
        *blue  = (unsigned int) round(value * 255.0);
        break;
      case 5:
        *red   = (unsigned int) round(value * 255.0);
        *green = (unsigned int) round(p * 255.0);
        *blue  = (unsigned int) round(q * 255.0);
        break;
    }
  }
}
