# Fritzing sketch arduino101 (saved by Fritzing 0.9.3b)
breadboards: 1

parts:
  Arduino_101 = Arduino 101
  LED1 = smd LED [color="Yellow (592nm)" package="1206 [SMD]"]
  R1 = Resistor [tolerance=±5% resistance=470 package="2010 [SMD]"]

nets:
  N1: Arduino_101.D13/SCK, LED1.anode
  N2: Arduino_101.GND, R1.Pin_0
  N3: LED1.cathode, R1.Pin_1

custom parts:
  Arduino 101: A learning and development board that delivers the performance and low-power consumption of the Intel® Curie™ Module with the simplicity of Arduino at an entry-level price. It keeps the same robust form factor and peripheral list of the UNO with the addition of onboard Bluetooth LE capabilities and a 6-axis accelerometer/gyro to help you easily expand your creativity into the connected world.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

// code stored in the sketch: arduino-led-9.ino
#include <CurieBLE.h>


const int pinLED = 9;

BLEPeripheral ble;
BLEService lightbulbService("8E76F000-690E-472E-88C3-051277686A73");
BLECharCharacteristic onCharacteristic("8E76F001-690E-472E-88C3-051277686A73", BLERead | BLEWrite);
BLEFloatCharacteristic brightnessCharacteristic("8E76F002-690E-472E-88C3-051277686A73", BLERead | BLEWrite);


void setup() {
  Serial.begin(115200);
  pinMode(pinLED, OUTPUT);

  ble.setLocalName("Arduino");
  ble.setAdvertisedServiceUuid(lightbulbService.uuid());

  ble.addAttribute(lightbulbService);
  ble.addAttribute(onCharacteristic);
  ble.addAttribute(brightnessCharacteristic);

  ble.setEventHandler(BLEConnected, onCentralConnect);
  ble.setEventHandler(BLEDisconnected, onCentralDisconnect);

  onCharacteristic.setValue(true);
  brightnessCharacteristic.setValue(100.0);
  setLED(true, 100.0);

  onCharacteristic.setEventHandler(BLEWritten, onCharacteristicWrite);
  brightnessCharacteristic.setEventHandler(BLEWritten, onCharacteristicWrite);
  
  
  ble.begin();
  Serial.println("Bluetooth on");
}

void loop() {
  ble.poll();
}


void onCentralConnect(BLECentral& central) {
  Serial.print("Central device connected: ");
  Serial.println(central.address());
}

void onCentralDisconnect(BLECentral& central) {
  Serial.print("Central device disconnected: ");
  Serial.println(central.address());
}

void onCharacteristicWrite(BLECentral& central, BLECharacteristic& characteristic) {
  Serial.print("Characteristic written: ");
  Serial.println(characteristic.uuid());

  bool state = (bool) onCharacteristic.value();
  float brightness = brightnessCharacteristic.value();
  setLED(state, brightness);
}

void setLED(bool state, float brightness) {
  const int analogMax = 255;
  brightness = max(0.0, min(100.0, brightness));  
 
  Serial.print("LED state: ");
  Serial.print(state);
  Serial.print("|");
  Serial.println(brightness);

  analogWrite(pinLED, int(state) * int(brightness / 100.0) * analogMax);
}

// code stored in the sketch: arduino-lightbulb.ino
#include <CurieBLE.h>


const int pinLED = 9;
const int pinSwitch = 2;

BLEPeripheral ble;
BLEService lightbulbService("8E76F000-690E-472E-88C3-051277686A73");
BLECharCharacteristic onCharacteristic("8E76F001-690E-472E-88C3-051277686A73", BLERead | BLEWrite | BLENotify);
BLEFloatCharacteristic brightnessCharacteristic("8E76F002-690E-472E-88C3-051277686A73", BLERead | BLEWrite | BLENotify);


void setup() {
  Serial.begin(115200);
  pinMode(pinLED, OUTPUT);
  pinMode(pinSwitch, INPUT_PULLUP);

  ble.setLocalName("Arduino");
  ble.setAdvertisedServiceUuid(lightbulbService.uuid());

  ble.addAttribute(lightbulbService);
  ble.addAttribute(onCharacteristic);
  ble.addAttribute(brightnessCharacteristic);

  ble.setEventHandler(BLEConnected, onCentralConnect);
  ble.setEventHandler(BLEDisconnected, onCentralDisconnect);

  onCharacteristic.setValue(true);
  brightnessCharacteristic.setValue(100.0);
  setLED(true, 100.0);
  attachInterrupt(digitalPinToInterrupt(pinSwitch), setSwitch, FALLING);

  onCharacteristic.setEventHandler(BLEWritten, onCharacteristicWrite);
  brightnessCharacteristic.setEventHandler(BLEWritten, onCharacteristicWrite);
  
  
  ble.begin();
  Serial.println("Bluetooth on");
}

void loop() {
  ble.poll();
}


void onCentralConnect(BLECentral& central) {
  Serial.print("Central device connected: ");
  Serial.println(central.address());
}

void onCentralDisconnect(BLECentral& central) {
  Serial.print("Central device disconnected: ");
  Serial.println(central.address());
}

void onCharacteristicWrite(BLECentral& central, BLECharacteristic& characteristic) {
  Serial.print("Characteristic written: ");
  Serial.println(characteristic.uuid());

  bool on = onCharacteristic.value();
  float brightness = brightnessCharacteristic.value();
  setLED(on, brightness);
}

void setLED(bool on, float brightness) {
  const int analogMax = 255;
  brightness = max(0.0, min(100.0, brightness));  
 
  Serial.print("LED state: ");
  Serial.print(on);
  Serial.print("|");
  Serial.println(brightness);

  analogWrite(pinLED, int(on) * int(brightness / 100.0) * analogMax);
}

void setSwitch(void) {
  Serial.println("Switch toggled");
  bool on = onCharacteristic.value();
  float brightness = brightnessCharacteristic.value();

  onCharacteristic.setValue(!on);
  setLED(!on, brightness);
}

// code stored in the sketch: arduino101.ino
#include <Arduino.h>
#include <CurieBLE.h>

const int pinLED = 13;


BLEPeripheral ble;
BLEService lightbulbService("8E76F000-690E-472E-88C3-051277686A73");
BLECharCharacteristic onCharacteristic("8E76F001-690E-472E-88C3-051277686A73", BLEWrite | BLERead | BLENotify);


void setup() {
  Serial.begin(115200);
  pinMode(pinLED, OUTPUT);

  ble.setLocalName("Light");
  ble.setAdvertisedServiceUuid(lightbulbService.uuid());

  ble.addAttribute(lightbulbService);
  ble.addAttribute(onCharacteristic);

  bool on = true;
  onCharacteristic.setValueLE(on);
  setLED(on);

  ble.setEventHandler(BLEConnected, onCentralConnect);
  ble.setEventHandler(BLEDisconnected, onCentralDisconnect);
  onCharacteristic.setEventHandler(BLEWritten, onCharacteristicWrite);

  ble.begin();
  Serial.println("Bluetooth on");
}

void loop() {
  ble.poll();
}


void onCentralConnect(BLECentral& central) {
  Serial.print("Central connected | ");
  Serial.println(central.address());
}

void onCentralDisconnect(BLECentral& central) {
  Serial.print("Central disconnected | ");
  Serial.println(central.address());
}

void onCharacteristicWrite(BLECentral& central, BLECharacteristic& characteristic) {
  Serial.print("Characteristic written | ");
  Serial.println(characteristic.uuid());

  bool on = (bool) onCharacteristic.valueLE();
  setLED(on);
}

void setLED(bool on) {
  Serial.print("LED | ");
  Serial.print(on);
  digitalWrite(pinLED, on);
}
