# Fritzing sketch arduino101 (saved by Fritzing 0.9.3b)
breadboards: 1

parts:
  Arduino_101 = Arduino 101
  S3 = Momentary Switch [package=ksa_sealed_tac_switch]

nets:
  N1: Arduino_101.GND, S3.4
  N2: Arduino_101.D2, S3.2

custom parts:
  Arduino 101: A learning and development board that delivers the performance and low-power consumption of the Intel® Curie™ Module with the simplicity of Arduino at an entry-level price. It keeps the same robust form factor and peripheral list of the UNO with the addition of onboard Bluetooth LE capabilities and a 6-axis accelerometer/gyro to help you easily expand your creativity into the connected world.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

// code stored in the sketch: arduino101.ino
#include <Arduino.h>
#include <CurieBLE.h>

const int pinSwitch = 2;


BLEPeripheral ble;
BLEService switchService("5ECEC5A0-7F71-41DA-9B8C-6252FE7EFB7E");
BLECharCharacteristic onCharacteristic("5ECEC5A1-7F71-41DA-9B8C-6252FE7EFB7E", BLEWrite | BLERead | BLENotify);
bool lastSwitch = HIGH;


void setup() {
  Serial.begin(115200);
  pinMode(pinSwitch, INPUT_PULLUP);

  ble.setLocalName("Switch");
  ble.setAdvertisedServiceUuid(switchService.uuid());

  ble.addAttribute(switchService);
  ble.addAttribute(onCharacteristic);
  onCharacteristic.setValueLE(false);

  ble.setEventHandler(BLEConnected, centralConnect);
  ble.setEventHandler(BLEDisconnected, centralDisconnect);
  onCharacteristic.setEventHandler(BLEWritten, characteristicWrite);

  ble.begin();
  Serial.println("Bluetooth on");
  lastSwitch = digitalRead(pinSwitch);
}

void loop() {
  ble.poll();

  if ((digitalRead(pinSwitch) == LOW) && (lastSwitch == HIGH)) {
    bool on = (bool) onCharacteristic.valueLE();
    onCharacteristic.setValue(!on);
    Serial.print("Switch | ");
    Serial.println(!on);
    ble.poll();
    lastSwitch = LOW;
    delay(1);
  } else if ((digitalRead(pinSwitch) == HIGH) && (lastSwitch == LOW)) {
    lastSwitch = HIGH;
    delay(1);
  }
}


void centralConnect(BLECentral& central) {
  Serial.print("Central connected | ");
  Serial.println(central.address());
}

void centralDisconnect(BLECentral& central) {
  Serial.print("Central disconnected | ");
  Serial.println(central.address());
}

void characteristicWrite(BLECentral& central, BLECharacteristic& characteristic) {
  Serial.print("Characteristic written | ");
  Serial.println(characteristic.uuid());

  bool on = (bool) onCharacteristic.valueLE();
  Serial.print("Switch | ");
  Serial.println(on);
}
